# Fritzing sketch sketch arduino mega (saved by Fritzing 0.9.3b)

parts:
  Componente3 = NRF24L01+ Breakout Board
  Componente4 = Arduino Mega 2560 (Rev3)

nets:
  GND: Componente3.GND, Componente4.GND
  VCC: Componente3.VCC, Componente4.3V3
  N1: Componente3.CE, Componente4.D9_PWM
  N2: Componente3.CS, Componente4.D10_PWM
  N3: Componente3.SCK, Componente4.D52
  N4: Componente3.MOSI, Componente4.D51
  N5: Componente3.MISO, Componente4.D50
