# Fritzing sketch sketch arduino uno (saved by Fritzing 0.9.3b)

parts:
  Componente1 = Arduino Uno (Rev3) - ICSP
  Componente2 = NRF24L01+ Breakout Board

nets:
  N1: Componente1.D9_PWM, Componente2.CE
  N2: Componente1.D10_PWM/SS, Componente2.CS
  N3: Componente1.D11_PWM/MOSI, Componente2.MOSI
  N4: Componente1.D12/MISO, Componente2.MISO
  N5: Componente1.D13/SCK, Componente2.SCK
  GND: Componente1.GND, Componente2.GND
  3V3: Componente1.3V3, Componente2.VCC
